// Digital circuit CPU.dig as structural Verilog
module CPU (
  input  [15:0] value,
  input  [1:0] dest,
  input  [1:0] src,
  input  tworeg,
  output [15:0] r0,
  output [15:0] r1,
  output [15:0] r2,
  output [15:0] r3,
  output [1:0] rd,
  output [1:0] rd_2,
  output [15:0] L,
  output [1:0] rs,
  output [15:0] target,
  output [3:0] PC,
  output [15:0] R
);

  wire add, add_out, assembler_1_p8, assembler_1_p9, decoder_1_p1, decoder_1_p2, fecthc_counter_1_p4,
       fecthc_counter_1_p7, jump, jump_out, mode_out, pm_1_p6, pm_1_p7, pm_1_p8;
  wire [3:0] pm_1_p4;
  wire [15:0] execute_1_result;
  wire [31:0] pm_1_p5, PROGRAM_d;

  LED programming (.in(mode_out));
  DipSwitch mode (.out(mode_out));
  Button u_add (.out(add_out));
  Button u_jump (.out(jump_out));
  // assembler assembler_1: pin names not known; wires that end beside it: mode_out, value, dest, src, tworeg, add_out, jump_out, assembler_1_p8, assembler_1_p9
  // PM pm_1: pin names not known; wires that end beside it: assembler_1_p8, assembler_1_p9, PC, pm_1_p4, pm_1_p5, pm_1_p6, pm_1_p7, pm_1_p8
  EEPROMDualPort #(.AddrBits(4), .Bits(32)) PROGRAM (
    .A(pm_1_p4), .Din(pm_1_p5), .str(pm_1_p6), .C(pm_1_p7), .ld(pm_1_p8), .D(PROGRAM_d));
  // fecthc_counter fecthc_counter_1: pin names not known; wires that end beside it: mode_out, assembler_1_p8, PROGRAM_d, fecthc_counter_1_p4, R, jump, fecthc_counter_1_p7, PC
  Button Advance (.out(fecthc_counter_1_p4));
  LED led_1 (.in(add));
  LED led_2 (.in(jump));
  // decoder decoder_1: pin names not known; wires that end beside it: decoder_1_p1, decoder_1_p2, fecthc_counter_1_p7, rs, rd, L, R, add, jump
  execute execute_1 (.A(L), .B(R), .add(add), .result(execute_1_result));
  // reg_file reg_file_1: pin names not known; wires that end beside it: rs, rd, execute_1_result, fecthc_counter_1_p4, decoder_1_p1, decoder_1_p2, r0, r1, r2, r3

  assign rd_2 = rd;
  assign target = R;

  // Notes on the sheet:
  //   value: default 1
  //   dest: default 1
  //   src: default 1
  //   tworeg: default 1
  //   0. R2=R2+1
  //   1. R2=R1+R2
  //   2. R3=R2+0
  //   3. R1=R1+R2
  //   4. R3=R1+0
  //   5. JUMP 1
  //   contents of PROGRAM (hex, n*v repeats v):
  //   220001,8120000,230000,8210000,130000,7000001
  //   jump
  //   add
  //   pc =
  //   R
  //   =
  //   (R               )
  //   +
endmodule
